// Logisim project ULA.circ as structural Verilog: 1 circuit, main circuit main
module main (
  input  in_1,
  input  in_2,
  input  in_3,
  input  in_4,
  input  in_5,
  input  in_6,
  input  in_7,
  input  in_8,
  input  in_9,
  input  in_10,
  input  in_11,
  input  in_12,
  input  in_13,
  input  in_14,
  input  in_15,
  input  in_16,
  input  in_17,
  input  in_18,
  input  in_19,
  input  in_20,
  input  in_21,
  input  in_22,
  input  in_23,
  input  in_24,
  input  in_25,
  input  in_26,
  input  in_27,
  input  in_28,
  input  in_29,
  input  in_30,
  input  in_31,
  input  in_32,
  input  in_33,
  input  in_34,
  input  in_35,
  input  in_36,
  input  in_37,
  input  in_38,
  input  in_39,
  input  in_40,
  input  in_41,
  input  in_42,
  input  in_43,
  input  in_44
);

  wire and_1_out, and_2_out, and_3_out, and_4_out, and_5_out, and_6_out, and_7_out, and_8_out, and_9_out,
       and_10_out, and_11_out, and_12_out, and_13_out, and_14_out, and_15_out, and_16_out, and_17_out,
       and_18_out, and_19_out, and_20_out, and_21_out, and_22_out, and_23_out, and_24_out, and_25_out,
       and_26_out, and_27_out, and_28_out, and_29_out, and_30_out, and_31_out, and_32_out, and_33_out,
       and_34_out, and_35_out, and_36_out, and_37_out, and_38_out, and_39_out, and_40_out, and_41_out,
       and_42_out, and_43_out, and_44_out, and_45_out, and_46_out, and_47_out, and_48_out, and_49_out,
       and_50_out, and_51_out, and_52_out, and_53_out, and_54_out, and_55_out, and_56_out, and_57_out,
       and_58_out, and_59_out, and_60_out, and_61_out, and_62_out, and_63_out, and_64_out, and_65_out,
       and_66_out, and_67_out, and_68_out, and_69_out, and_70_out, and_71_out, not_1_out, not_2_out,
       not_3_out, not_4_out, not_5_out, not_6_out, not_7_out, not_8_out, not_9_out, not_10_out, not_11_out,
       not_12_out, not_13_out, not_14_out, not_15_out, not_16_out, not_17_out, not_18_out, not_19_out,
       not_20_out, not_21_out, or_1_out, or_2_out, or_3_out, or_4_out, or_5_out, or_6_out, or_7_out,
       or_8_out, or_9_out, or_10_out, or_11_out, or_12_out, or_13_out, or_14_out, or_15_out, or_16_out,
       or_17_out, xor_1_out, xor_2_out, xor_3_out, xor_4_out, xor_5_out, xor_6_out, xor_7_out, xor_8_out,
       xor_9_out, xor_10_out, xor_11_out, xor_12_out, xor_13_out, xor_14_out, xor_15_out, xor_16_out,
       xor_17_out, xor_18_out, xor_19_out, xor_20_out, xor_21_out, xor_22_out, xor_23_out, xor_24_out,
       xor_25_out, xor_26_out, xor_27_out;

  and and_1 (and_1_out, in_4, in_8);
  and and_2 (and_2_out, in_3, in_7);
  and and_3 (and_3_out, in_2, in_6);
  and and_4 (and_4_out, in_1, in_5);
  or or_1 (or_1_out, in_4, in_8);
  or or_2 (or_2_out, in_3, in_7);
  or or_3 (or_3_out, in_2, in_6);
  or or_4 (or_4_out, in_1, in_5);
  xor xor_1 (xor_1_out, in_4, in_8);
  xor xor_2 (xor_2_out, in_3, in_7);
  xor xor_3 (xor_3_out, in_2, in_6);
  xor xor_4 (xor_4_out, in_1, in_5);
  and and_5 (and_5_out, in_4, xor_15_out);
  or or_5 (or_5_out, and_5_out, and_12_out);
  and and_6 (and_6_out, in_3, xor_16_out);
  or or_6 (or_6_out, and_6_out, and_13_out);
  and and_7 (and_7_out, in_2, xor_17_out);
  or or_7 (or_7_out, and_7_out, and_14_out);
  and and_8 (and_8_out, in_1, xor_18_out);
  or or_8 (or_8_out, and_8_out, and_15_out);
  xor xor_5 (xor_5_out, 1'b1, in_4);
  and and_9 (and_9_out, 1'b1, in_4);
  not not_1 (not_1_out, xor_4_out);
  not not_2 (not_2_out, xor_3_out);
  not not_3 (not_3_out, xor_2_out);
  not not_4 (not_4_out, xor_1_out);
  and and_10 (and_10_out, in_2, ~in_6, not_1_out);  // AND_Gate
  and and_11 (and_11_out, in_1, ~in_5);  // AND_Gate
  xor xor_6 (xor_6_out, xor_15_out, in_4);
  and and_12 (and_12_out, xor_6_out, and_21_out);
  xor xor_7 (xor_7_out, and_21_out, xor_6_out);
  xor xor_8 (xor_8_out, xor_16_out, in_3);
  and and_13 (and_13_out, xor_8_out, or_5_out);
  xor xor_9 (xor_9_out, or_5_out, xor_8_out);
  xor xor_10 (xor_10_out, xor_17_out, in_2);
  and and_14 (and_14_out, xor_10_out, or_6_out);
  xor xor_11 (xor_11_out, or_6_out, xor_10_out);
  xor xor_12 (xor_12_out, xor_18_out, in_1);
  and and_15 (and_15_out, xor_12_out, or_7_out);
  xor xor_13 (xor_13_out, or_7_out, xor_12_out);
  xor xor_14 (xor_14_out, and_9_out, in_3);
  and and_16 (and_16_out, and_9_out, in_3);
  and and_17 (and_17_out, not_4_out, not_3_out, not_2_out, not_1_out);
  and and_18 (and_18_out, in_4, ~in_8, not_3_out, not_2_out, not_1_out);  // AND_Gate
  and and_19 (and_19_out, in_3, ~in_7, not_2_out, not_1_out);  // AND_Gate
  xor xor_15 (xor_15_out, in_8, and_21_out);
  xor xor_16 (xor_16_out, in_7, and_21_out);
  xor xor_17 (xor_17_out, in_6, and_21_out);
  xor xor_18 (xor_18_out, in_5, and_21_out);
  and and_20 (and_20_out, and_16_out, in_2);
  or or_9 (or_9_out, and_18_out, and_19_out, and_10_out, and_11_out);
  and and_21 (and_21_out, ~in_10, in_9, in_11);  // AND_Gate
  xor xor_19 (xor_19_out, and_16_out, in_2);
  xor xor_20 (xor_20_out, and_21_out, or_8_out);
  xor xor_21 (xor_21_out, and_20_out, in_1);
  and and_22 (and_22_out, and_20_out, in_1);
  not not_5 (not_5_out, in_10);
  not not_6 (not_6_out, in_9);
  not not_7 (not_7_out, in_10);
  not not_8 (not_8_out, in_9);
  not not_9 (not_9_out, in_10);
  not not_10 (not_10_out, in_9);
  not not_11 (not_11_out, in_10);
  not not_12 (not_12_out, in_9);
  not not_13 (not_13_out, in_11);
  not not_14 (not_14_out, in_11);
  not not_15 (not_15_out, in_11);
  not not_16 (not_16_out, in_11);
  and and_23 (and_23_out, and_1_out, not_13_out, not_5_out, not_6_out);
  and and_24 (and_24_out, xor_1_out, not_13_out, in_10, not_6_out);
  and and_25 (and_25_out, xor_7_out, not_13_out, not_5_out, in_9);
  and and_26 (and_26_out, xor_5_out, not_13_out, in_10, in_9);
  and and_27 (and_27_out, and_2_out, not_14_out, not_7_out, not_8_out);
  and and_28 (and_28_out, xor_2_out, not_14_out, in_10, not_8_out);
  and and_29 (and_29_out, xor_9_out, not_14_out, not_7_out, in_9);
  and and_30 (and_30_out, xor_14_out, not_14_out, in_10, in_9);
  and and_31 (and_31_out, and_3_out, not_15_out, not_9_out, not_10_out);
  and and_32 (and_32_out, xor_3_out, not_15_out, in_10, not_10_out);
  and and_33 (and_33_out, xor_11_out, not_15_out, not_9_out, in_9);
  and and_34 (and_34_out, xor_19_out, not_15_out, in_10, in_9);
  and and_35 (and_35_out, and_4_out, not_16_out, not_11_out, not_12_out);
  and and_36 (and_36_out, xor_4_out, not_16_out, in_10, not_12_out);
  and and_37 (and_37_out, xor_13_out, not_16_out, not_11_out, in_9);
  and and_38 (and_38_out, xor_21_out, not_16_out, in_10, in_9);
  and and_39 (and_39_out, or_1_out, in_11, not_5_out, not_6_out);
  and and_40 (and_40_out, in_4, in_11, in_10, not_6_out);
  and and_41 (and_41_out, xor_7_out, in_11, not_5_out, in_9);
  and and_42 (and_42_out, 1'b0, in_11, in_10, in_9);
  and and_43 (and_43_out, or_2_out, in_11, not_7_out, not_8_out);
  and and_44 (and_44_out, in_3, in_11, in_10, not_8_out);
  and and_45 (and_45_out, xor_9_out, in_11, not_7_out, in_9);
  and and_46 (and_46_out, 1'b0, in_11, in_10, in_9);
  and and_47 (and_47_out, or_3_out, in_11, not_9_out, not_10_out);
  and and_48 (and_48_out, in_2, in_11, in_10, not_10_out);
  and and_49 (and_49_out, xor_11_out, in_11, not_9_out, in_9);
  and and_50 (and_50_out, 1'b0, in_11, in_10, in_9);
  and and_51 (and_51_out, or_4_out, in_11, not_11_out, not_12_out);
  and and_52 (and_52_out, in_1, in_11, in_10, not_12_out);
  and and_53 (and_53_out, xor_13_out, in_11, not_11_out, in_9);
  and and_54 (and_54_out, 1'b0, in_11, in_10, in_9);
  and and_55 (and_55_out, ~in_11, in_10, in_9, and_22_out);  // AND_Gate
  or or_10 (or_10_out, and_23_out, and_39_out, and_24_out, and_40_out, and_25_out, and_41_out, and_26_out, and_42_out);
  or or_11 (or_11_out, and_27_out, and_43_out, and_28_out, and_44_out, and_29_out, and_45_out, and_30_out, and_46_out);
  or or_12 (or_12_out, and_31_out, and_47_out, and_32_out, and_48_out, and_33_out, and_49_out, and_34_out, and_50_out);
  or or_13 (or_13_out, and_35_out, and_51_out, and_36_out, and_52_out, and_37_out, and_53_out, and_38_out, and_54_out);
  or or_14 (or_14_out, and_55_out, xor_20_out);
  LED led_1 (.in(or_13_out));
  LED led_2 (.in(or_12_out));
  LED led_3 (.in(or_11_out));
  LED led_4 (.in(or_10_out));
  LED led_5 (.in(or_14_out));
  LED led_6 (.in(and_17_out));
  LED led_7 (.in(or_9_out));
  LED led_8 (.in(and_56_out));
  and and_56 (and_56_out, ~or_10_out, ~or_11_out, ~or_12_out, ~or_13_out);  // AND_Gate
  and and_57 (and_57_out, in_16, in_18);
  or or_15 (or_15_out, in_25, in_27);
  xor xor_22 (xor_22_out, 1'b1, in_39);
  and and_58 (and_58_out, 1'b1, in_39);
  LED led_9 (.in(in_32));
  LED led_10 (.in(and_58_out));
  LED led_11 (.in(and_57_out));
  LED led_12 (.in(or_15_out));
  LED led_13 (.in(in_33));
  LED led_14 (.in(in_34));
  LED led_15 (.in(in_35));
  LED led_16 (.in(xor_22_out));
  and and_59 (and_59_out, ~in_41, ~in_42, ~in_43, ~in_44);  // AND_Gate
  xor xor_23 (xor_23_out, in_17, in_19);
  not not_17 (not_17_out, in_40);
  not not_18 (not_18_out, xor_23_out);
  and and_60 (and_60_out, in_30, ~in_36);  // AND_Gate
  LED led_17 (.in(xor_23_out));
  LED led_18 (.in(not_18_out));
  LED led_19 (.in(and_60_out));
  LED led_20 (.in(not_17_out));
  LED led_21 (.in(and_59_out));
  and and_61 (and_61_out, in_20, xor_26_out);
  or or_16 (or_16_out, and_61_out, and_62_out);
  xor xor_24 (xor_24_out, xor_26_out, in_20);
  and and_62 (and_62_out, xor_24_out, in_22);
  xor xor_25 (xor_25_out, in_22, xor_24_out);
  xor xor_26 (xor_26_out, in_21, in_22);
  LED led_22 (.in(xor_25_out));
  xor xor_27 (xor_27_out, or_16_out, in_22);
  LED led_23 (.in(xor_27_out));
  not not_19 (not_19_out, in_12);
  not not_20 (not_20_out, in_13);
  not not_21 (not_21_out, in_14);
  and and_63 (and_63_out, in_23, not_21_out, not_20_out, not_19_out);
  and and_64 (and_64_out, in_26, not_21_out, in_13, not_19_out);
  and and_65 (and_65_out, in_29, not_21_out, not_20_out, in_12);
  and and_66 (and_66_out, in_37, not_21_out, in_13, in_12);
  and and_67 (and_67_out, in_24, in_14, not_20_out, not_19_out);
  and and_68 (and_68_out, in_28, in_14, in_13, not_19_out);
  and and_69 (and_69_out, in_31, in_14, not_20_out, in_12);
  and and_70 (and_70_out, in_38, in_14, in_13, in_12);
  LED led_24 (.in(and_71_out));
  and and_71 (and_71_out, ~in_15, or_17_out);  // AND_Gate
  or or_17 (or_17_out, and_63_out, and_67_out, and_64_out, and_68_out, and_65_out, and_69_out, and_66_out, and_70_out);

  // Notes on the sheet:
  //   AND
  //   OR
  //   ADD / SUB
  //   XOR
  //   A=B
  //   A>B
  //   A
  //   INC A
  //   SUB BIT
  //   8 x 1 MUX
  //   8 x 1 MUX
  //   8 x 1 MUX
  //   8 x 1 MUX
  //   Carry Filter
  //   S3
  //   S2
  //   S1
  //   S0
  //   CARRY
  //   A = B
  //   A > B
  //   ZERO
  //   1 Bit - Incrementer
  //   Carry
  //   1 Bit - AND
  //   1 Bit - OR
  //   4 Bit - A
  //   FLAG - ZERO 1 Bit
  //   FLAG - ZERO 4Bits
  //   1 Bit - XOR
  //   FLAG - A = B
  //   FLAG - A > B
  //   1 Bit - ADD / SUB
  //   Carry
  //   8x1 MUX
endmodule
